# Fritzing sketch Saw-Tri_WaveShaper+Amp_PreBuffer (saved by Fritzing 0.9.4)
breadboards: 1

parts:
  IC1 = Dual Op-Amp [package=dip08]
  C1 = Ceramic Capacitor [capacitance=100nF package="100 mil [THT, multilayer]"]
  C2 = Ceramic Capacitor [capacitance=100nF package="100 mil [THT, multilayer]"]
  R1 = Resistor [tolerance=±5% resistance=100k package=THT]
  C3 = Ceramic Capacitor [capacitance=100nF package="100 mil [THT, multilayer]"]
  R2 = Resistor [tolerance=±5% resistance=470k package=THT]
  R3 = Resistor [tolerance=±5% resistance=150k package=THT]
  Q1 = NPN-Transistor [package="TO92 [THT]"]
  R4 = Resistor [tolerance=±5% resistance=10k package=THT]
  R5 = Resistor [tolerance=±5% resistance=10k package=THT]
  R6 = TRIMPOT [package=trimpot_pth_s3_lock]
  C4 = Electrolytic Capacitor [capacitance=1µF package="100 mil [THT, electrolytic]"]
  C5 = Electrolytic Capacitor [capacitance=1µF package="100 mil [THT, electrolytic]"]
  R7 = Resistor [tolerance=±5% resistance=2.2k package=THT]

nets:
  N1: IC1.A_OUT, IC1.A_-IN, Q1.C
  N2: IC1.A_+IN, R7.Pin_0
  N3: IC1.A_V-, C2.0, R4.Pin_1, C5.-
  N4: IC1.B_+IN, Q1.B, R5.Pin_0
  N5: IC1.B_-IN, R1.Pin_1, C3.1, R2.Pin_1, R3.Pin_0
  N6: IC1.B_OUT, R1.Pin_0, C3.0
  N7: IC1.A_V+, C1.0, R6.WIPER, R6.CW, C4.+
  N8: C1.1, C2.1, R2.Pin_0, C4.-, C5.+
  N9: Q1.E, R4.Pin_0
  N10: R5.Pin_1, R6.CCW

notes:
  +5V
  GND
  +12V
  -12V
  GND
  TRI_OUT
  5K
  Trim
  SAW_IN
