# Fritzing sketch Saw-Tri_WaveShaper (saved by Fritzing 0.9.4)
breadboards: 1

parts:
  Q1 = NPN-Transistor [package="TO92 [THT]"]
  R1 = Resistor [tolerance=±5% resistance=10k package=THT]
  R2 = TRIMPOT [package=trimpot_pth_s3_lock]
  R3 = Resistor [tolerance=±5% resistance=10k package=THT]
  C1 = Electrolytic Capacitor [capacitance=1µF package="100 mil [THT, electrolytic]"]
  C2 = Electrolytic Capacitor [capacitance=1µF package="100 mil [THT, electrolytic]"]

nets:
  N1: Q1.E, R3.Pin_0
  N2: Q1.B, Q1.C, R1.Pin_0
  N3: R1.Pin_1, R2.CCW
  N4: R2.WIPER, R2.CW, C1.+
  N5: R3.Pin_1, C2.-
  N6: C1.-, C2.+

notes:
  TRI_OUT
  SAW_IN
  GND
  +12V
  -12V
  GND
  5k Trim
